# Fritzing sketch Kaipod2 (saved by Fritzing 0.9.3b)

parts:
  Raspberry_Pi_1 = Raspberry Pi 3 [part_number=RPI-3-V1.2]  # not connected
  Part1 = Adafruit PowerBoost 1000C [part_number="Adafruit #2465"]
  S1 = Taiway 100-SP-X-T1 SPDT Miniature Toggle Switch [part_number=100-SP-X-T1-0-0-B1-M2 package=THT]
  U1 = LIPO-2000mAh [package=lipo-2000]  # not connected
  Part3 = Adafruit Pi Cobbler [part_number="Adafruit #914"]
  Part4 = Adafruit Stereo 2.1W Class D Audio Amplifier - TPA2012 [part_number="Adafruit #1552"]
  SP1 = SPEAKER [package=pcb_mount_speaker]
  SP2 = SPEAKER [package=pcb_mount_speaker]
  Part5 = 3.5in TFT 480x320 Touch + MicroSD  # not connected
  Previous = Arcade Button (blue)
  Play/Pause = Arcade Button (blue)
  Next = Arcade Button (blue)
  Volume_Up = Arcade Button (white)  # not connected
  Volume_Down = Arcade Button (white)
  3_5mm_TRS_Switching_Jack = AUDIO-JACK2 [package=audio-jack]
  Part6 = TRRS 3.5mm Jack Breakout

nets:
  N1: Part1.ENABLE, S1.L1
  N2: Part1.GND, S1.L2
  N3: Part3.SDA, Play/Pause.no_name_yet
  N4: Part3.5.0V, Part4.VDD
  N5: Part3.SCL, Previous.no_name_yet
  GND: Part3.GND, Part4.GND, Volume_Down.no_name_yet#2
  N6: Part3.GPIO4, Next.no_name_yet
  N7: Part4.OUT_LEFT-, SP2.+
  N8: Part4.OUT_LEFT+, SP2.-
  N9: Part4.OUT_RIGHT+, SP1.-
  N10: Part4.OUT_RIGHT-, SP1.+
  N11: Part4.IN_RIGHT+, 3_5mm_TRS_Switching_Jack.RSH
  N12: Part4.IN_RIGHT-, Part4.IN_LEFT-
  N13: Part4.IN_LEFT+, 3_5mm_TRS_Switching_Jack.TIP
  N14: 3_5mm_TRS_Switching_Jack.RING, Part6.RING2
  N15: 3_5mm_TRS_Switching_Jack.SLEEVE, Part6.SLEEVE
  N16: 3_5mm_TRS_Switching_Jack.TSH, Part6.TIP

notes:
  Powerboost 1000c connected to Raspberry Pi with Micro USB power cable
  PiTFT Plus connected with ribbon cable to Raspberry Pi
  Using this object to illustrate the 13x2 GPIO pinout of the PiTFT Plus
  These buttons for volume are connected to the solder pads on the rear of the PiTFT+ Pad 5 and Pad 6
  Imagine this is a PLUG not a jack that goes into the audio jack of the Raspberry Pi

custom parts:
  Adafruit PowerBoost 1000C: PowerBoost 1000C is the perfect power supply for your portable project! With a built-in load-sharing battery charger circuit, you'll be able to keep your power-hungry project running even while recharging the battery! This little DC/DC boost converter module can be powered by any 3.7V LiIon/LiPoly battery, and convert the battery output to 5.2V DC for running your 5V projects.
  Adafruit Pi Cobbler: Now that you've finally got your hands on a Raspberry Pi® Model B , you're probably itching to make some fun embedded computer projects with it. What you need is an add on prototyping Pi Cobbler from Adafruit, which can break out all those tasty power, GPIO, I2C and SPI pins from the 26 pin header onto a solderless breadboard. This set will make "cobbling together" prototypes with the Pi super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
  Adafruit Stereo 2.1W Class D Audio Amplifier - TPA2012: This incredibly small stereo amplifier is surprisingly powerful - able to deliver 2 x 2.1W channels into 4 ohm impedance speakers (@ 10% THD). Inside the miniature chip is a class D controller, able to run from 2.7V-5.5VDC. Since the amp is a class D, it's incredibly efficient (89% efficient when driving an 8Ω speaker at 1.5 Watt) - making it perfect for portable and battery-powered projects.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
  3.5in TFT 480x320 Touch + MicroSD: This TFT display is big (3.5" diagonal), bright (6 white-LED backlight) and colorful! 480x320 pixels with individual RGB pixel control. This display also has a resistive touchscreen attached to it already, so you can detect finger presses anywhere on the screen. There is a controller built into the display with RAM buffering, so that almost no work is done by the microcontroller. The display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
  Arcade Button (blue): Adafruit Arcade Button (blue)
  Arcade Button (white): Adafruit Arcade Button (white)
